# Fritzing sketch final_step (saved by Fritzing 0.9.3b)
breadboards: 1

parts:
  Part1 = Arduino Uno (Rev3) - ICSP  # not connected
  Part2 = Arduino Ethernet Shield (Rev3)
  Q1 = Basic FET N-Channel [package="TO220 [THT]"]
  R1 = Resistor [tolerance=±5% resistance=1k package=THT]
  R2 = Resistor [tolerance=±5% resistance=1M package="0402 [SMD]"]
  R3 = Resistor [tolerance=±5% resistance=1M package="0402 [SMD]"]
  Part3 = Soil Moisture Sensor
  Part4 = Soil Moisture Sensor
  S1 = Tilt Switch [package=THT]
  R4 = Resistor [tolerance=±5% resistance=1k package="0603 [SMD]"]
  M1 = DC Motor

nets:
  VCC: Part2.5V, Part3.VCC, Part4.VCC, R4.Pin_1
  N1: Part2.A0, R2.Pin_0, Part3.SIG
  N2: Part2.A1, R3.Pin_0, Part4.SIG
  N3: Part2.D2, Q1.gate, R1.Pin_1
  N4: Part2.PWM_D3, S1.Pin_1, R4.Pin_0
  GND: Part2.GND, Q1.source, R1.Pin_0, R2.Pin_1, R3.Pin_1, Part3.GND, Part4.GND, S1.Pin_2
  N5: Part2.VIN, M1.pin_2
  N6: Q1.drain, M1.pin_1

notes:
  Pump
  Sensor 1
  Sensor 2
  Float
  This rail is connected to Vin
  This rail is connected to 5V
