# Fritzing sketch mosfet (saved by Fritzing 0.9.3b)
breadboards: 1

parts:
  Part1 = Arduino Uno (Rev3) - ICSP  # not connected
  Part2 = Arduino Ethernet Shield (Rev3)
  R1 = Resistor [tolerance=±5% resistance=1k package=THT]
  M1 = DC Motor
  Q1 = Basic FET N-Channel [package="TO220 [THT]"]

nets:
  N1: Part2.D2, R1.Pin_1, Q1.gate
  N2: Part2.GND, R1.Pin_0, Q1.source
  N3: Part2.VIN, M1.pin_2
  N4: M1.pin_1, Q1.drain

notes:
  Pump
  This rail is connected to Vin
