# Fritzing sketch project (saved by Fritzing 0.9.3b)
breadboards: 1

parts:
  Part1 = Arduino Uno (Rev3) - ICSP  # not connected
  Part2 = Arduino Ethernet Shield (Rev3)
  Q1 = Basic FET N-Channel [package="TO220 [THT]"]
  R1 = Resistor [tolerance=±5% resistance=1k package=THT]
  M1 = DC Motor

nets:
  N1: Part2.D2, Q1.gate, R1.Pin_1
  N2: Part2.GND, Q1.source, R1.Pin_0
  N3: Part2.VIN, M1.pin_2
  N4: Q1.drain, M1.pin_1

notes:
  Pump
  This rail is connected to Vin
