# Fritzing sketch project (saved by Fritzing 0.9.3b)
breadboards: 1

parts:
  Part1 = Arduino Uno (Rev3) - ICSP  # not connected
  Part2 = Arduino Ethernet Shield (Rev3)
  LED2 = LED - 5mm [color="Red (633nm)" package="5 mm [THT]"]
  LED3 = LED - 5mm [color="Blue (430nm)" package="5 mm [THT]"]
  LED4 = LED - 5mm [color="Green (555nm)" package="5 mm [THT]"]
  LED5 = LED - 5mm [color="Yellow (585nm)" package="5 mm [THT]"]
  R1 = Resistor [tolerance=±5% resistance=220 package=THT]
  R2 = Resistor [tolerance=±5% resistance=220 package=THT]
  R3 = Resistor [tolerance=±5% resistance=220 package=THT]
  R4 = Resistor [tolerance=±5% resistance=220 package=THT]
  S1 = SWITCH-MOMENTARY-2 [package=tactile-pth-12mm]
  S2 = SWITCH-MOMENTARY-2 [package=tactile-pth-12mm]
  S3 = SWITCH-MOMENTARY-2 [package=tactile-pth-12mm]
  S4 = SWITCH-MOMENTARY-2 [package=tactile-pth-12mm]
  R5 = Resistor [tolerance=±5% resistance=1k package=THT]
  R6 = Resistor [tolerance=±5% resistance=1k package=THT]
  R7 = Resistor [tolerance=±5% resistance=1k package=THT]
  R8 = Resistor [tolerance=±5% resistance=1k package=THT]

nets:
  N1: Part2.D8, R3.Pin_1
  N2: Part2.PWM_D9, R4.Pin_1
  N3: Part2.GND, LED2.cathode, LED3.cathode, LED4.cathode, LED5.cathode, S1.2, S2.2, S3.2, S4.2
  N4: Part2.D2, S4.1, R8.Pin_0
  N5: Part2.PWM_D3, S3.1, R7.Pin_0
  N6: Part2.SDCS, S2.1, R6.Pin_0
  N7: Part2.PWM_D5, S1.1, R5.Pin_0
  N8: Part2.PWM_D6, R1.Pin_1
  N9: Part2.D7, R2.Pin_1
  N10: Part2.5V, R5.Pin_1, R6.Pin_1, R7.Pin_1, R8.Pin_1
  N11: LED2.anode, R4.Pin_0
  N12: LED3.anode, R1.Pin_0
  N13: LED4.anode, R2.Pin_0
  N14: LED5.anode, R3.Pin_0
