# Fritzing sketch fritzing (saved by Fritzing 0.9.3b)
breadboards: 2

parts:
  U1 = NodeMCU V1.0
  Part1 = RFID-RC522-v2

nets:
  N1: U1.D3, Part1.RST
  3V3: U1.3V3, Part1.3.3V
  GND: U1.GND, Part1.GND
  N2: U1.D5, Part1.SCK
  N3: U1.D6, Part1.MISO
  N4: U1.D7, Part1.MOSI
  N5: U1.D8, Part1.SDA

custom parts:
  NodeMCU V1.0: ESP8266 based NodeMCU
  RFID-RC522-v2: A simple China made RFID-RC522 Reader; do check the pin labels, as this is a MFRC522 based clone.
